// Logisim project 32x16 RAM.circ as structural Verilog: 6 circuits, main circuit 8x1 RAM
module _8x1_RAM (
  input  INPUT,
  input  RESET,
  input  SAVE,
  input  A0,
  input  A1,
  input  A2,
  output out_7
);

  wire d_ff_1_q, d_ff_2_q, d_ff_3_q, d_ff_4_q, d_ff_5_q, d_ff_6_q, d_ff_7_q, d_ff_8_q, demultiplexer_1_out0,
       demultiplexer_1_out1, demultiplexer_1_out2, demultiplexer_1_out3, demultiplexer_1_out4,
       demultiplexer_1_out5, demultiplexer_1_out6, demultiplexer_1_out7;

  Demultiplexer #(.select(3)) demultiplexer_1 (
    .out0(demultiplexer_1_out0), .out1(demultiplexer_1_out1), .out2(demultiplexer_1_out2),
    .out3(demultiplexer_1_out3), .out4(demultiplexer_1_out4), .out5(demultiplexer_1_out5),
    .out6(demultiplexer_1_out6), .out7(demultiplexer_1_out7), .in(SAVE), .sel({A2, A1, A0}));  // open: en
  D_Flip_Flop d_ff_1 (.clk(demultiplexer_1_out0), .D(INPUT), .Q(d_ff_1_q), .reset(RESET));  // open: Qn, preset, en
  D_Flip_Flop d_ff_2 (.clk(demultiplexer_1_out1), .D(INPUT), .Q(d_ff_2_q), .reset(RESET));  // open: Qn, preset, en
  D_Flip_Flop d_ff_3 (.clk(demultiplexer_1_out2), .D(INPUT), .Q(d_ff_3_q), .reset(RESET));  // open: Qn, preset, en
  D_Flip_Flop d_ff_4 (.clk(demultiplexer_1_out3), .D(INPUT), .Q(d_ff_4_q), .reset(RESET));  // open: Qn, preset, en
  D_Flip_Flop d_ff_5 (.clk(demultiplexer_1_out4), .D(INPUT), .Q(d_ff_5_q), .reset(RESET));  // open: Qn, preset, en
  D_Flip_Flop d_ff_6 (.clk(demultiplexer_1_out5), .D(INPUT), .Q(d_ff_6_q), .reset(RESET));  // open: Qn, preset, en
  D_Flip_Flop d_ff_7 (.clk(demultiplexer_1_out6), .D(INPUT), .Q(d_ff_7_q), .reset(RESET));  // open: Qn, preset, en
  D_Flip_Flop d_ff_8 (.clk(demultiplexer_1_out7), .D(INPUT), .Q(d_ff_8_q), .reset(RESET));  // open: Qn, preset, en
  Multiplexer #(.select(3)) multiplexer_1 (
    .in0(d_ff_1_q), .in1(d_ff_2_q), .in2(d_ff_3_q), .in3(d_ff_4_q), .in4(d_ff_5_q), .in5(d_ff_6_q),
    .in6(d_ff_7_q), .in7(d_ff_8_q), .out(out_7), .sel({A2, A1, A0}));  // open: en

  // Notes on the sheet:
  //   ADRESS
  //   8x1 RAM
endmodule

module _8x2_RAM (
  input  [1:0] INPUT,
  input  R,
  input  S,
  input  A0,
  input  A1,
  input  A2,
  output [1:0] out_7
);

  _8x1_RAM u_8x1_ram_1 (.INPUT(INPUT[0]), .RESET(R), .SAVE(S), .out_7(out_7[0]), .A0(A0), .A1(A1), .A2(A2));
  _8x1_RAM u_8x1_ram_2 (.INPUT(INPUT[1]), .RESET(R), .SAVE(S), .out_7(out_7[1]), .A0(A0), .A1(A1), .A2(A2));

  // Notes on the sheet:
  //   8x2 RAM
endmodule

module _16x1_RAM (
  input  IN,
  input  S,
  input  A0,
  input  A1,
  input  A2,
  input  A3,
  output out_7
);

  wire demultiplexer_1_out0, demultiplexer_1_out1, n8x1_ram_1_out_7, n8x1_ram_2_out_7;

  Demultiplexer demultiplexer_1 (
    .out0(demultiplexer_1_out0), .out1(demultiplexer_1_out1), .in(S), .sel(A3));  // open: en
  _8x1_RAM u_8x1_ram_1 (
    .INPUT(IN), .SAVE(demultiplexer_1_out0), .out_7(n8x1_ram_1_out_7), .A0(A0), .A1(A1), .A2(A2));  // open: RESET
  _8x1_RAM u_8x1_ram_2 (
    .INPUT(IN), .SAVE(demultiplexer_1_out1), .out_7(n8x1_ram_2_out_7), .A0(A0), .A1(A1), .A2(A2));  // open: RESET
  Multiplexer multiplexer_1 (.in0(n8x1_ram_1_out_7), .in1(n8x1_ram_2_out_7), .out(out_7), .sel(A3));  // open: en
endmodule

module _32x1_RAM (
  input  IN,
  input  S,
  input  A0,
  input  A1,
  input  A2,
  input  A3,
  input  A4,
  output out_8
);

  wire demultiplexer_1_out0, demultiplexer_1_out1, n16x1_ram_1_out_7, n16x1_ram_2_out_7;

  Demultiplexer demultiplexer_1 (
    .out0(demultiplexer_1_out0), .out1(demultiplexer_1_out1), .in(S), .sel(A4));  // open: en
  _16x1_RAM u_16x1_ram_1 (
    .IN(IN), .S(demultiplexer_1_out0), .A0(A0), .A1(A1), .A2(A2), .A3(A3), .out_7(n16x1_ram_1_out_7));
  _16x1_RAM u_16x1_ram_2 (
    .IN(IN), .S(demultiplexer_1_out1), .A0(A0), .A1(A1), .A2(A2), .A3(A3), .out_7(n16x1_ram_2_out_7));
  Multiplexer multiplexer_1 (.in0(n16x1_ram_1_out_7), .in1(n16x1_ram_2_out_7), .out(out_8), .sel(A4));  // open: en

  // Notes on the sheet:
  //   32x1 RAM
endmodule

module _32x2_RAM (
  input  IN0,
  input  IN1,
  input  S,
  input  A0,
  input  A1,
  input  A2,
  input  A3,
  input  A4,
  output out_9,
  output out_10
);

  _32x1_RAM u_32x1_ram_1 (.IN(IN0), .S(S), .A0(A0), .A1(A1), .A2(A2), .A3(A3), .A4(A4), .out_8(out_9));
  _32x1_RAM u_32x1_ram_2 (.IN(IN1), .S(S), .A0(A0), .A1(A1), .A2(A2), .A3(A3), .A4(A4), .out_8(out_10));

  // Notes on the sheet:
  //   32x2 RAM
endmodule

module _32x16_RAM (
  input  [15:0] in_1,
  input  S,
  input  A0,
  input  A1,
  input  A2,
  input  A3,
  input  A4,
  output [15:0] out_8
);

  _32x2_RAM u_32x2_ram_1 (
    .IN0(in_1[1]), .IN1(in_1[0]), .S(S), .A0(A0), .A1(A1), .A2(A2), .A3(A3), .A4(A4), .out_10(out_8[0]),
    .out_9(out_8[1]));
  _32x2_RAM u_32x2_ram_2 (
    .IN0(in_1[3]), .IN1(in_1[2]), .S(S), .A0(A0), .A1(A1), .A2(A2), .A3(A3), .A4(A4), .out_10(out_8[2]),
    .out_9(out_8[3]));
  _32x2_RAM u_32x2_ram_3 (
    .IN0(in_1[5]), .IN1(in_1[4]), .S(S), .A0(A0), .A1(A1), .A2(A2), .A3(A3), .A4(A4), .out_10(out_8[4]),
    .out_9(out_8[5]));
  _32x2_RAM u_32x2_ram_4 (
    .IN0(in_1[7]), .IN1(in_1[6]), .S(S), .A0(A0), .A1(A1), .A2(A2), .A3(A3), .A4(A4), .out_10(out_8[6]),
    .out_9(out_8[7]));
  _32x2_RAM u_32x2_ram_5 (
    .IN0(in_1[9]), .IN1(in_1[8]), .S(S), .A0(A0), .A1(A1), .A2(A2), .A3(A2), .A4(A4), .out_10(out_8[8]),
    .out_9(out_8[9]));
  _32x2_RAM u_32x2_ram_6 (
    .IN0(in_1[11]), .IN1(in_1[10]), .S(S), .A0(A0), .A1(A1), .A2(A2), .A3(A3), .A4(A4), .out_10(out_8[10]),
    .out_9(out_8[11]));
  _32x2_RAM u_32x2_ram_7 (
    .IN0(in_1[13]), .IN1(in_1[12]), .S(S), .A0(A0), .A1(A1), .A2(A2), .A3(A3), .A4(A4), .out_10(out_8[12]),
    .out_9(out_8[13]));
  _32x2_RAM u_32x2_ram_8 (
    .IN0(in_1[15]), .IN1(in_1[14]), .S(S), .A0(A0), .A1(A1), .A2(A2), .A3(A3), .A4(A4), .out_10(out_8[14]),
    .out_9(out_8[15]));

  // Notes on the sheet:
  //   IN
  //   32x16 RAM
endmodule
