// Logisim project 4 - битный мультиплексор.circ as structural Verilog: 1 circuit, main circuit main
module main (
  input  [4:0] in_1,
  input  in_2,
  input  [4:0] in_3,
  output [4:0] \ВЫХОД 
);

  wire and_1_out, and_2_out, and_3_out, and_4_out, and_5_out, and_6_out, and_7_out, and_8_out, and_9_out,
       and_10_out, not_1_out;

  not not_1 (not_1_out, in_2);
  and and_1 (and_1_out, in_1[0], not_1_out);
  and and_2 (and_2_out, in_1[1], not_1_out);
  and and_3 (and_3_out, in_1[2], not_1_out);
  and and_4 (and_4_out, in_1[3], not_1_out);
  and and_5 (and_5_out, in_1[4], not_1_out);
  and and_6 (and_6_out, in_3[0], in_2);
  and and_7 (and_7_out, in_3[1], in_2);
  and and_8 (and_8_out, in_3[2], in_2);
  and and_9 (and_9_out, in_3[3], in_2);
  and and_10 (and_10_out, in_3[4], in_2);
  or or_1 (\ВЫХОД [0], and_1_out, and_6_out);
  or or_2 (\ВЫХОД [1], and_2_out, and_7_out);
  or or_3 (\ВЫХОД [2], and_3_out, and_8_out);
  or or_4 (\ВЫХОД [3], and_4_out, and_9_out);
  or or_5 (\ВЫХОД [4], and_5_out, and_10_out);

  // Notes on the sheet:
  //   СИГНАЛ 0
  //   СЕЛЕКТОР
  //   СИГНАЛ 1
  //   МУЛЬТИПЛЕКСОР (MUX)
endmodule
