// Logisim project 8 - битный регистр.circ as structural Verilog: 1 circuit, main circuit main
module main (
  input  [7:0] in_1,
  output [7:0] out_2
);

  wire button_1_out, button_2_out, clock_1_out;

  Button button_1 (.out(button_1_out));
  Clock clock_1 (.out(clock_1_out));
  Button button_2 (.out(button_2_out));
  D_Flip_Flop d_ff_1 (
    .clk(clock_1_out), .D(in_1[0]), .Q(out_2[0]), .en(button_1_out), .reset(button_2_out));  // open: Qn, preset
  D_Flip_Flop d_ff_2 (
    .clk(clock_1_out), .D(in_1[1]), .Q(out_2[1]), .en(button_1_out), .reset(button_2_out));  // open: Qn, preset
  D_Flip_Flop d_ff_3 (
    .clk(clock_1_out), .D(in_1[2]), .Q(out_2[2]), .en(button_1_out), .reset(button_2_out));  // open: Qn, preset
  D_Flip_Flop d_ff_4 (
    .clk(clock_1_out), .D(in_1[3]), .Q(out_2[3]), .en(button_1_out), .reset(button_2_out));  // open: Qn, preset
  D_Flip_Flop d_ff_5 (
    .clk(clock_1_out), .D(in_1[4]), .Q(out_2[4]), .en(button_1_out), .reset(button_2_out));  // open: Qn, preset
  D_Flip_Flop d_ff_6 (
    .clk(clock_1_out), .D(in_1[5]), .Q(out_2[5]), .en(button_1_out), .reset(button_2_out));  // open: Qn, preset
  D_Flip_Flop d_ff_7 (
    .clk(clock_1_out), .D(in_1[6]), .Q(out_2[6]), .en(button_1_out), .reset(button_2_out));  // open: Qn, preset
  D_Flip_Flop d_ff_8 (
    .clk(clock_1_out), .D(in_1[7]), .Q(out_2[7]), .en(button_1_out), .reset(button_2_out));  // open: Qn, preset

  // Notes on the sheet:
  //   INPUT
  //   SAVE
  //   RESET
  //   8 - БИТНЫЙ РЕГИСТР
  //   DATA
endmodule
