// Logisim project 8 - битный сумматор с памятью.circ as structural Verilog: 1 circuit, main circuit main
module main (
  input  [7:0] in_1,
  input  [7:0] in_2,
  input  in_3,
  output [7:0] out_4,
  output [7:0] out_5
);

  wire button_1_out, button_2_out, clock_1_out;
  wire [7:0] multiplexer_1_out;

  Multiplexer #(.width(8), .enable("false")) multiplexer_1 (
    .in0(in_1), .in1(out_5), .out(multiplexer_1_out), .sel(in_3));
  Adder adder_1 (.a(multiplexer_1_out), .b(in_2), .out(out_4), .cin(1'b0));  // open: cout
  Button button_1 (.out(button_1_out));
  Clock clock_1 (.out(clock_1_out));
  Button button_2 (.out(button_2_out));
  Register register_1 (.D(out_4), .en(button_1_out), .Q(out_5), .clk(clock_1_out), .clr(button_2_out));

  // Notes on the sheet:
  //   IN 1
  //   IN 2
  //   SAVE
  //   RESET
  //   8 - БИТНЫЙ СУММАТОР С ПАМЯТЬЮ
  //   RESULT
  //   ПАМЯТЬ
endmodule
