// Logisim project 8 - битный сумматор-вычитатель .circ as structural Verilog: 1 circuit, main circuit main
module main (
  input  [7:0] input_1,
  input  [7:0] input_2,
  input  in_3,
  output [8:0] out_4
);

  wire adder_1_cout, adder_2_cout, adder_3_cout, adder_4_cout, adder_5_cout, adder_6_cout, adder_7_cout,
       adder_8_cout, xor_1_out, xor_2_out, xor_3_out, xor_4_out, xor_5_out, xor_6_out, xor_7_out, xor_8_out;

  xor xor_1 (xor_1_out, input_2[0], in_3);
  xor xor_2 (xor_2_out, input_2[1], in_3);
  xor xor_3 (xor_3_out, input_2[2], in_3);
  xor xor_4 (xor_4_out, input_2[3], in_3);
  xor xor_5 (xor_5_out, input_2[4], in_3);
  xor xor_6 (xor_6_out, input_2[5], in_3);
  xor xor_7 (xor_7_out, input_2[6], in_3);
  xor xor_8 (xor_8_out, input_2[7], in_3);
  Adder #(.width(1)) adder_1 (.a(input_1[0]), .b(xor_1_out), .out(out_4[0]), .cin(in_3), .cout(adder_1_cout));
  Adder #(.width(1)) adder_2 (.a(input_1[1]), .b(xor_2_out), .out(out_4[1]), .cin(adder_1_cout), .cout(adder_2_cout));
  Adder #(.width(1)) adder_3 (.a(input_1[2]), .b(xor_3_out), .out(out_4[2]), .cin(adder_2_cout), .cout(adder_3_cout));
  Adder #(.width(1)) adder_4 (.a(input_1[3]), .b(xor_4_out), .out(out_4[3]), .cin(adder_3_cout), .cout(adder_4_cout));
  Adder #(.width(1)) adder_5 (.a(input_1[4]), .b(xor_5_out), .out(out_4[4]), .cin(adder_4_cout), .cout(adder_5_cout));
  Adder #(.width(1)) adder_6 (.a(input_1[5]), .b(xor_6_out), .out(out_4[5]), .cin(adder_5_cout), .cout(adder_6_cout));
  Adder #(.width(1)) adder_7 (.a(input_1[6]), .b(xor_7_out), .out(out_4[6]), .cin(adder_6_cout), .cout(adder_7_cout));
  Adder #(.width(1)) adder_8 (.a(input_1[7]), .b(xor_8_out), .out(out_4[7]), .cin(adder_7_cout), .cout(adder_8_cout));
  xor xor_9 (out_4[8], adder_8_cout, in_3);

  // Notes on the sheet:
  //   1 - "-"  \ 0 - "+"
  //   8 - битный сумматор-вычитатель
  //   out
endmodule
