// Logisim project 8 - битный сумматор.circ as structural Verilog: 1 circuit, main circuit main
module main (
  input  in_1,
  input  in_2,
  input  in_3,
  input  input_1,
  input  in_5,
  input  in_6,
  input  in_7,
  input  in_8,
  input  in_9,
  input  in_10,
  input  in_11,
  input  input_2,
  input  in_13,
  input  in_14,
  input  in_15,
  input  in_16,
  output out_17,
  output out_18,
  output out_19,
  output sum,
  output out_21,
  output out_22,
  output out_23,
  output out_24,
  output out_25
);

  wire adder_1_cout, adder_2_cout, adder_3_cout, adder_4_cout, adder_5_cout, adder_6_cout, adder_7_cout;

  Adder #(.width(1)) adder_1 (.a(in_16), .b(in_8), .out(out_25), .cout(adder_1_cout));  // open: cin
  Adder #(.width(1)) adder_2 (.a(in_15), .b(in_7), .out(out_24), .cin(adder_1_cout), .cout(adder_2_cout));
  Adder #(.width(1)) adder_3 (.a(in_14), .b(in_6), .out(out_23), .cin(adder_2_cout), .cout(adder_3_cout));
  Adder #(.width(1)) adder_4 (.a(in_13), .b(in_5), .out(out_22), .cin(adder_3_cout), .cout(adder_4_cout));
  Adder #(.width(1)) adder_5 (.a(input_2), .b(input_1), .out(out_21), .cin(adder_4_cout), .cout(adder_5_cout));
  Adder #(.width(1)) adder_6 (.a(in_11), .b(in_3), .out(sum), .cin(adder_5_cout), .cout(adder_6_cout));
  Adder #(.width(1)) adder_7 (.a(in_10), .b(in_2), .out(out_19), .cin(adder_6_cout), .cout(adder_7_cout));
  Adder #(.width(1)) adder_8 (.a(in_9), .b(in_1), .out(out_18), .cin(adder_7_cout), .cout(out_17));

  // Notes on the sheet:
  //   Восьмибитный сумматор
endmodule
