// Logisim project 8x1 RAM.circ as structural Verilog: 1 circuit, main circuit main
module main (
  input  INPUT,
  input  [2:0] ADRESS,
  output out_3
);

  wire button_1_out, button_2_out, d_ff_1_q, d_ff_2_q, d_ff_3_q, d_ff_4_q, d_ff_5_q, d_ff_6_q, d_ff_7_q,
       d_ff_8_q, demultiplexer_1_out0, demultiplexer_1_out1, demultiplexer_1_out2, demultiplexer_1_out3,
       demultiplexer_1_out4, demultiplexer_1_out5, demultiplexer_1_out6, demultiplexer_1_out7;

  Button button_1 (.out(button_1_out));
  Button button_2 (.out(button_2_out));
  Demultiplexer #(.select(3)) demultiplexer_1 (
    .out0(demultiplexer_1_out0), .out1(demultiplexer_1_out1), .out2(demultiplexer_1_out2),
    .out3(demultiplexer_1_out3), .out4(demultiplexer_1_out4), .out5(demultiplexer_1_out5),
    .out6(demultiplexer_1_out6), .out7(demultiplexer_1_out7), .in(button_2_out), .sel(ADRESS));  // open: en
  D_Flip_Flop d_ff_1 (
    .clk(demultiplexer_1_out0), .D(INPUT), .Q(d_ff_1_q), .reset(button_1_out));  // open: Qn, preset, en
  D_Flip_Flop d_ff_2 (
    .clk(demultiplexer_1_out1), .D(INPUT), .Q(d_ff_2_q), .reset(button_1_out));  // open: Qn, preset, en
  D_Flip_Flop d_ff_3 (
    .clk(demultiplexer_1_out2), .D(INPUT), .Q(d_ff_3_q), .reset(button_1_out));  // open: Qn, preset, en
  D_Flip_Flop d_ff_4 (
    .clk(demultiplexer_1_out3), .D(INPUT), .Q(d_ff_4_q), .reset(button_1_out));  // open: Qn, preset, en
  D_Flip_Flop d_ff_5 (
    .clk(demultiplexer_1_out4), .D(INPUT), .Q(d_ff_5_q), .reset(button_1_out));  // open: Qn, preset, en
  D_Flip_Flop d_ff_6 (
    .clk(demultiplexer_1_out5), .D(INPUT), .Q(d_ff_6_q), .reset(button_1_out));  // open: Qn, preset, en
  D_Flip_Flop d_ff_7 (
    .clk(demultiplexer_1_out6), .D(INPUT), .Q(d_ff_7_q), .reset(button_1_out));  // open: Qn, preset, en
  D_Flip_Flop d_ff_8 (
    .clk(demultiplexer_1_out7), .D(INPUT), .Q(d_ff_8_q), .reset(button_1_out));  // open: Qn, preset, en
  Multiplexer #(.select(3)) multiplexer_1 (
    .in0(d_ff_1_q), .in1(d_ff_2_q), .in2(d_ff_3_q), .in3(d_ff_4_q), .in4(d_ff_5_q), .in5(d_ff_6_q),
    .in6(d_ff_7_q), .in7(d_ff_8_q), .out(out_3), .sel(ADRESS));  // open: en

  // Notes on the sheet:
  //   RESET
  //   SAVE
  //   8x1 RAM
endmodule
