// Logisim project Microprocessor systems.circ as structural Verilog
module ALU_with_flags (
  input  [7:0] input_1,
  input  [7:0] input_2,
  input  commutator_1,
  input  [2:0] commutator_2,
  output overflow,
  output out_6,
  output out_7,
  output negative,
  output [7:0] \output ,
  output zero_flag,
  output out_11
);

  wire adder_1_cout, subtractor_1_bout;
  wire [7:0] adder_1_out, and_1_out, divider_1_out, input2, multiplier, multiplier_1_out, not_1_out,
       or_1_out, subtractor_1_out, xor_1_out;

  // Probe on input_2
  // Probe on input_1
  Multiplexer #(.width(8)) multiplexer_1 (
    .in0(input_2), .in1(not_1_out), .out(input2), .sel(commutator_1));  // open: en
  assign not_1_out = ~input_2;  // NOT_Gate not_1, 8 bits wide
  Adder_part adder_1 (.a(input_1), .b(input2), .out(adder_1_out), .cout(adder_1_cout));  // open: cin
  Subtractor subtractor_1 (.a(input_1), .b(input2), .out(subtractor_1_out), .bout(subtractor_1_bout));  // open: bin
  Multiplier multiplier_1 (.a(input_1), .b(input2), .out(multiplier_1_out), .cout(multiplier));  // open: cin
  Divider divider_1 (.a(input_1), .b(input2), .out(divider_1_out));  // open: upper, rem
  assign and_1_out = input_1 & input2;  // AND_Gate and_1, 8 bits wide
  assign or_1_out = input_1 | input2;  // OR_Gate or_1, 8 bits wide
  assign xor_1_out = input_1 ^ input2;  // XOR_Gate xor_1, 8 bits wide
  Multiplexer #(.select(3), .width(8)) multiplexer_2 (
    .in0(adder_1_out), .in1(subtractor_1_out), .in2(multiplier_1_out), .in3(divider_1_out), .in4(and_1_out),
    .in5(or_1_out), .in6(xor_1_out), .in7(input2), .out(\output ), .sel(commutator_2));  // open: en
  Comparator #(.mode("unsigned")) comparator_1 (.a(\output ), .b({8{1'b0}}), .gt(out_6), .eq(out_7), .lt(negative));
  or or_2 (out_11, \output [0], \output [1], \output [2], \output [3], \output [4], \output [5], \output [6], \output [7]);
  or or_3 (overflow, adder_1_cout, multiplier[0], multiplier[1], multiplier[2], multiplier[3], multiplier[4], multiplier[5], multiplier[6], multiplier[7]);
  // Probe on \output 
  not not_2 (zero_flag, out_11);

  // Other names for the same wires on the sheet: input1[7:0] = input_1

  // Notes on the sheet:
  //   ALU
endmodule

module Harvard_architecture (
);

  wire A_or_S, and_1_out, and_2_out, and_3_out, clear_out, clock_1_out, not_1_out, or_1_out, write;
  wire [7:0] adder_1_out, counter_1_q, multiplexer_1_out, multiplexer_2_out, ram_1_data, ram_2_data,
       register_1_q, subtractor_1_out;

  // Probe on counter_1_q
  not not_1 (not_1_out, ram_1_data[3]);
  Clock clock_1 (.out(clock_1_out));
  Button clear (.out(clear_out));
  Counter counter_1 (
    .load(ram_1_data[3]), .D(ram_2_data), .count(not_1_out), .Q(counter_1_q), .clk(clock_1_out),
    .clr(clear_out));  // open: carry
  RAM ram_1 (.addr(counter_1_q), .data({ram_1_data[7:3], A_or_S, ram_1_data[1:0]}));  // open: sel, clk, ld, clr
  RAM #(.bus("separate")) ram_2 (
    .addr(counter_1_q), .din(register_1_q), .data(ram_2_data), .clk(write));  // open: str, sel, ld, clr
  // Probe on multiplexer_1_out
  Adder_part adder_1 (.a(register_1_q), .b(ram_2_data), .out(adder_1_out));  // open: cin, cout
  Multiplexer #(.width(8)) multiplexer_1 (
    .in0(adder_1_out), .in1(subtractor_1_out), .out(multiplexer_1_out), .sel(A_or_S));  // open: en
  Subtractor subtractor_1 (.a(register_1_q), .b(ram_2_data), .out(subtractor_1_out));  // open: bin, bout
  // Probe on multiplexer_2_out
  Multiplexer #(.width(8)) multiplexer_2 (
    .in0(multiplexer_1_out), .in1(ram_2_data), .out(multiplexer_2_out), .sel(ram_1_data[0]));  // open: en
  and and_1 (and_1_out, clock_1_out, ram_1_data[0]);
  and and_2 (and_2_out, clock_1_out, ram_1_data[1]);
  and and_3 (and_3_out, clock_1_out, A_or_S);
  and and_4 (write, clock_1_out, ram_1_data[4]);
  // Probe on register_1_q
  Register register_1 (.D(multiplexer_2_out), .Q(register_1_q), .clk(or_1_out), .clr(clear_out));  // open: en
  or or_1 (or_1_out, and_1_out, and_2_out, and_3_out);

  // Notes on the sheet:
  //   Load 01
  //   Sum 02
  //   Sub 04
  //   Jump 08
  //   Write 10
  //   Commands:
  //   Harvard architecture
endmodule

module Semi_adder (
  input  input_1,
  input  input_2,
  output overflow,
  output sum
);

  and and_1 (overflow, input_1, input_2);
  xor xor_1 (sum, input_1, input_2);

  // Notes on the sheet:
  //   Semi adder
endmodule

module Adder (
  input  input_1,
  input  input_2,
  input  transition_bit,
  output overflow,
  output sum
);

  wire and_1_out, and_2_out, xor_1_out;

  xor xor_1 (xor_1_out, input_1, input_2);
  and and_1 (and_1_out, input_1, input_2);
  xor xor_2 (sum, xor_1_out, transition_bit);
  and and_2 (and_2_out, xor_1_out, transition_bit);
  or or_1 (overflow, and_1_out, and_2_out);

  // Notes on the sheet:
  //   Adder
endmodule

module _4_bit_1_bit_adder (
  input  transition_bit,
  input  [3:0] input_1,
  input  [3:0] input_2,
  output [4:0] out_4
);

  wire adder_2_overflow, adder_3_overflow, adder_4_overflow;

  Adder adder_1 (
    .input_1(input_1[3]), .input_2(input_2[3]), .transition_bit(adder_2_overflow), .overflow(out_4[4]),
    .sum(out_4[3]));
  Adder adder_2 (
    .input_1(input_1[2]), .input_2(input_2[2]), .transition_bit(adder_3_overflow),
    .overflow(adder_2_overflow), .sum(out_4[2]));
  Adder adder_3 (
    .input_1(input_1[1]), .input_2(input_2[1]), .transition_bit(adder_4_overflow),
    .overflow(adder_3_overflow), .sum(out_4[1]));
  Adder adder_4 (
    .input_1(input_1[0]), .input_2(input_2[0]), .transition_bit(transition_bit), .overflow(adder_4_overflow),
    .sum(out_4[0]));

  // Notes on the sheet:
  //   4-bit 1-bit adder
endmodule

module _8_bit_register_from_D_flip_flops (
  input  [7:0] \input ,
  output [7:0] \output 
);

  wire clear, clock_out;

  Button clock (.out(clock_out));
  Button u_clear (.out(clear));
  D_Flip_Flop d_ff_1 (.clk(clock_out), .D(\input [0]), .Q(\output [0]), .reset(clear));  // open: Qn, preset, en
  D_Flip_Flop d_ff_2 (.clk(clock_out), .D(\input [1]), .Q(\output [1]), .reset(clear));  // open: Qn, preset, en
  D_Flip_Flop d_ff_3 (.clk(clock_out), .D(\input [2]), .Q(\output [2]), .reset(clear));  // open: Qn, preset, en
  D_Flip_Flop d_ff_4 (.clk(clock_out), .D(\input [3]), .Q(\output [3]), .reset(clear));  // open: Qn, preset, en
  D_Flip_Flop d_ff_5 (.clk(clock_out), .D(\input [4]), .Q(\output [4]), .reset(clear));  // open: Qn, preset, en
  D_Flip_Flop d_ff_6 (.clk(clock_out), .D(\input [5]), .Q(\output [5]), .reset(clear));  // open: Qn, preset, en
  D_Flip_Flop d_ff_7 (.clk(clock_out), .D(\input [6]), .Q(\output [6]), .reset(clear));  // open: Qn, preset, en
  D_Flip_Flop d_ff_8 (.clk(clock_out), .D(\input [7]), .Q(\output [7]), .reset(clear));  // open: Qn, preset, en

  // Notes on the sheet:
  //   8-bit register from D-flip-flops
endmodule

module Adder_with_the_ability_to_remember (
  input  [7:0] input_1,
  input  [7:0] input_2,
  input  commutator,
  output [7:0] \output ,
  output [7:0] memory
);

  wire clock_out, reset_out;
  wire [7:0] multiplexer_1_out;

  Multiplexer #(.width(8)) multiplexer_1 (
    .in0(input_2), .in1(memory), .out(multiplexer_1_out), .sel(commutator));  // open: en
  Adder_part adder_1 (.a(input_1), .b(multiplexer_1_out), .out(\output ), .cin(1'b0));  // open: cout
  Button clock (.out(clock_out));
  Button reset (.out(reset_out));
  Register register_1 (.D(\output ), .Q(memory), .clk(clock_out), .clr(reset_out));  // open: en

  // Notes on the sheet:
  //   Adder with the ability to remember
endmodule

module Adder_with_possibility_of_subtraction (
  input  [7:0] input_1,
  input  [7:0] input_2,
  input  commutator,
  output [7:0] \output 
);

  wire adder_1_cout, and_1_out;
  wire [7:0] multiplexer_1_out, not_1_out;

  // Probe on input_1
  // Probe on input_2
  assign not_1_out = ~input_2;  // NOT_Gate not_1, 8 bits wide
  Multiplexer #(.width(8)) multiplexer_1 (
    .in0(input_2), .in1(not_1_out), .out(multiplexer_1_out), .sel(commutator));  // open: en
  and and_1 (and_1_out, commutator, adder_1_cout);
  // Probe on \output 
  Adder_part adder_1 (.a(input_1), .b(multiplexer_1_out), .out(\output ), .cin(and_1_out), .cout(adder_1_cout));

  // Notes on the sheet:
  //   Adder with possibility of subtraction
endmodule

module _4_bit_register (
  input  [3:0] \input ,
  output [3:0] memory
);

  wire clear_out, clock_out;

  Button clock (.out(clock_out));
  Button clear (.out(clear_out));
  D_Flip_Flop d_ff_1 (.clk(clock_out), .D(\input [0]), .Q(memory[0]), .reset(clear_out));  // open: Qn, preset, en
  D_Flip_Flop d_ff_2 (.clk(clock_out), .D(\input [1]), .Q(memory[1]), .reset(clear_out));  // open: Qn, preset, en
  D_Flip_Flop d_ff_3 (.clk(clock_out), .D(\input [2]), .Q(memory[2]), .reset(clear_out));  // open: Qn, preset, en
  D_Flip_Flop d_ff_4 (.clk(clock_out), .D(\input [3]), .Q(memory[3]), .reset(clear_out));  // open: Qn, preset, en

  // Notes on the sheet:
  //   4-bit register
endmodule

module Memory_from_4_register (
  input  [7:0] \input ,
  input  [1:0] commutator,
  output [7:0] memory
);

  wire clock_out, demultiplexer_1_out0, demultiplexer_1_out1, demultiplexer_1_out2, demultiplexer_1_out3;
  wire [7:0] register_1_q, register_2_q, register_3_q, register_4_q;

  Register register_1 (.D(\input ), .Q(register_1_q), .clk(demultiplexer_1_out0));  // open: en, clr
  Register register_2 (.D(\input ), .Q(register_2_q), .clk(demultiplexer_1_out1));  // open: en, clr
  Register register_3 (
    .D(\input ), .Q(register_3_q), .clk(demultiplexer_1_out2), .clr(demultiplexer_1_out2));  // open: en
  Register register_4 (.D(\input ), .Q(register_4_q), .clk(demultiplexer_1_out3));  // open: en, clr
  Button clock (.out(clock_out));
  Demultiplexer #(.select(2)) demultiplexer_1 (
    .out0(demultiplexer_1_out0), .out1(demultiplexer_1_out1), .out2(demultiplexer_1_out2),
    .out3(demultiplexer_1_out3), .in(clock_out), .sel(commutator));  // open: en
  Multiplexer #(.select(2), .width(8)) multiplexer_1 (
    .in0(register_1_q), .in1(register_2_q), .in2(register_3_q), .in3(register_4_q), .out(memory),
    .sel(commutator));  // open: en

  // Notes on the sheet:
  //   Memory from 4 register
endmodule

module Counter_from_D_flip_flop (
);

  wire clock_1_out, d_ff_1_q, d_ff_1_qn, d_ff_2_q, d_ff_2_qn, d_ff_3_q, d_ff_3_qn;

  Clock clock_1 (.out(clock_1_out));
  // Probe on d_ff_1_q
  D_Flip_Flop d_ff_1 (.clk(clock_1_out), .D(d_ff_1_qn), .Q(d_ff_1_q), .Qn(d_ff_1_qn));  // open: preset, en, reset
  // Probe on d_ff_2_q
  D_Flip_Flop d_ff_2 (.clk(d_ff_1_qn), .D(d_ff_2_qn), .Q(d_ff_2_q), .Qn(d_ff_2_qn));  // open: preset, en, reset
  // Probe on d_ff_3_q
  D_Flip_Flop d_ff_3 (.clk(d_ff_2_qn), .D(d_ff_3_qn), .Q(d_ff_3_q), .Qn(d_ff_3_qn));  // open: preset, en, reset

  // Notes on the sheet:
  //   Counter from D-flip-flop
endmodule

module out__command_compiler (
  input  [6:0] o,
  input  [6:0] u,
  input  [6:0] t,
  output flag
);

  wire and_1_out, and_2_out, clear_out, clock_out, comparator_1_eq, comparator_2_eq, comparator_3_eq,
       d_ff_1_q, d_ff_2_q;
  wire [6:0] keyboard_1_data;

  Button clock (.out(clock_out));
  Keyboard keyboard_1 (.clk(clock_out), .data(keyboard_1_data));  // open: re, clr, avail
  // Probe on keyboard_1_data
  Comparator #(.width(7)) comparator_1 (.a(keyboard_1_data), .b(o), .eq(comparator_1_eq));  // open: gt, lt
  Comparator #(.width(7)) comparator_2 (.a(keyboard_1_data), .b(u), .eq(comparator_2_eq));  // open: gt, lt
  Comparator #(.width(7)) comparator_3 (.a(keyboard_1_data), .b(t), .eq(comparator_3_eq));  // open: gt, lt
  TTY tty_1 (.data(keyboard_1_data), .clk(clock_out), .clr(clear_out));  // open: we
  and and_1 (and_1_out, d_ff_1_q, comparator_2_eq);
  and and_2 (and_2_out, d_ff_2_q, comparator_3_eq);
  D_Flip_Flop d_ff_1 (.clk(clock_out), .D(comparator_1_eq), .Q(d_ff_1_q));  // open: Qn, preset, en, reset
  D_Flip_Flop d_ff_2 (.clk(clock_out), .D(and_1_out), .Q(d_ff_2_q));  // open: Qn, preset, en, reset
  D_Flip_Flop d_ff_3 (.clk(clock_out), .D(and_2_out), .Q(flag));  // open: Qn, preset, en, reset
  Button clear (.out(clear_out));

  // Notes on the sheet:
  //   "o" - 1101111
  //   "u" - 1110101
  //   "t" - 1110100
  //   "out" command compiler
endmodule

module Von_Neumann_architecture (
);

  wire and_1_out, and_2_out, clock_1_out, not_1_out, not_2_out;
  wire [3:0] Adress_q, counter_1_q, Instruction_q, multiplexer_1_out;
  wire [7:0] Accum_q, adder_1_out, multiplexer_2_out, ram_1_data, Temp_q;

  Clock clock_1 (.out(clock_1_out));
  not not_1 (not_1_out, clock_1_out);
  Counter #(.width(4), .max('hf)) counter_1 (
    .load(Instruction_q[3]), .D(Adress_q), .count(not_2_out), .Q(counter_1_q), .clk(clock_1_out));  // open: carry, clr
  not not_2 (not_2_out, Instruction_q[3]);
  Multiplexer #(.width(4)) multiplexer_1 (
    .in0(counter_1_q), .out(multiplexer_1_out), .sel(not_1_out));  // open: in1, en
  RAM #(.addrWidth(4), .bus("separate")) ram_1 (
    .addr(multiplexer_1_out), .data(ram_1_data), .clk(and_1_out));  // open: din, str, sel, ld, clr
  and and_1 (and_1_out, clock_1_out, Instruction_q[1]);
  Register #(.width(4)) Instruction (.D(ram_1_data[7:4]), .Q(Instruction_q), .clk(not_1_out));  // open: en, clr
  Register #(.width(4)) Adress (.D(ram_1_data[3:0]), .Q(Adress_q), .clk(not_1_out));  // open: en, clr
  Register #(.trigger("falling")) Temp (.D(ram_1_data), .Q(Temp_q), .clk(and_2_out));  // open: en, clr
  and and_2 (and_2_out, Instruction_q[0], not_1_out);
  Adder_part adder_1 (.a(Accum_q), .b(Temp_q), .out(adder_1_out));  // open: cin, cout
  Multiplexer #(.width(8)) multiplexer_2 (
    .in0(adder_1_out), .in1(Temp_q), .out(multiplexer_2_out), .sel(Instruction_q[2]));  // open: en
  Register Accum (.D(multiplexer_2_out), .Q(Accum_q), .clk(clock_1_out));  // open: en, clr
  // Probe on Accum_q

  // Notes on the sheet:
  //   0 - загрузка в Temp
  //   1 - обновление памяти
  //   3 - безусловный переход
  //   2 - суммирование через Adder
  //   Von Neumann architecture
endmodule
