// Logisim project RS-D flip-flop.circ as structural Verilog: 1 circuit, main circuit main
module main (
  input  S,
  input  R,
  input  D,
  output nQ,
  output Q,
  output nQ_2,
  output Q_2
);

  wire and_1_out, and_2_out, button_1_out, button_2_out;

  Button button_1 (.out(button_1_out));
  Button button_2 (.out(button_2_out));
  and and_1 (and_1_out, button_1_out, D);
  and and_2 (and_2_out, D, button_2_out);
  nor nor_1 (nQ, S, Q);
  nor nor_2 (Q, nQ, R);
  nor nor_3 (nQ_2, and_1_out, Q_2);
  nor nor_4 (Q_2, nQ_2, and_2_out);

  // Notes on the sheet:
  //   S
  //   R
  //   RS - TRIGGER
  //   D - TRIGGER
endmodule
