// Logisim project Вывод цифры.circ as structural Verilog: 3 circuits, main circuit main
module main (
);

  wire _0_out, _1_out, _2_out, _3_out, _4_out, _5_out, _6_out, _7_out, _8_out, _9_out, cd_1_y0, cd_1_y1,
       cd_1_y2, cd_1_y3, dc_1_y0, dc_1_y1, dc_1_y2, dc_1_y3, dc_1_y4, dc_1_y5, dc_1_y6, dc_1_y7;

  Button _0 (.out(_0_out));
  Button _1 (.out(_1_out));
  Button _2 (.out(_2_out));
  Button _3 (.out(_3_out));
  Button _4 (.out(_4_out));
  Button _5 (.out(_5_out));
  Button _6 (.out(_6_out));
  Button _7 (.out(_7_out));
  Button _8 (.out(_8_out));
  Button _9 (.out(_9_out));
  CD cd_1 (
    .x0(_0_out), .x1(_1_out), .x2(_2_out), .x3(_3_out), .x4(_4_out), .x5(_5_out), .x6(_6_out), .x7(_7_out),
    .x8(_8_out), .x9(_9_out), .y3(cd_1_y3), .y2(cd_1_y2), .y1(cd_1_y1), .y0(cd_1_y0));
  DC dc_1 (
    .x3(cd_1_y3), .x2(cd_1_y2), .x1(cd_1_y1), .x0(cd_1_y0), .y0(dc_1_y0), .y1(dc_1_y1), .y2(dc_1_y2),
    .y3(dc_1_y3), .y4(dc_1_y4), .y5(dc_1_y5), .y6(dc_1_y6), .y7(dc_1_y7));
  _7_Segment_Display u_7_segment_display_1 (
    .g(dc_1_y0), .f(dc_1_y1), .a(dc_1_y2), .b(dc_1_y3), .e(dc_1_y4), .d(dc_1_y5), .c(dc_1_y6), .dp(dc_1_y7));

  // Notes on the sheet:
  //   0 = 01111110
  //   1 = 00010010
  //   2 = 10111100
  //   3 = 10110110
  //   4 = 11010010
  //   5 = 11100110
  //   6 = 11101110
  //   7 = 00110010
  //   8 = 11111110
  //   9 = 11110110
  //   НЕЙТРАЛКА = 10000001
endmodule

module DC (
  input  x3,
  input  x2,
  input  x1,
  input  x0,
  output y0,
  output y1,
  output y2,
  output y3,
  output y4,
  output y5,
  output y6,
  output y7
);

  wire and_1_out, and_2_out, and_3_out, and_4_out, and_5_out, and_6_out, and_7_out, and_8_out, and_9_out,
       and_10_out, and_11_out, and_12_out, and_13_out, and_14_out, and_15_out, and_16_out, and_17_out,
       and_18_out, and_19_out, and_20_out, and_21_out, and_22_out, and_23_out, and_24_out, and_25_out,
       and_26_out, and_27_out, and_28_out, and_29_out, and_30_out, and_31_out, and_32_out, not_1_out,
       not_2_out, not_3_out, not_4_out, not_5_out, not_6_out, not_7_out, not_8_out, not_9_out, not_10_out,
       not_11_out, not_12_out, not_13_out, not_14_out, not_15_out, not_16_out, not_17_out, not_18_out,
       not_19_out, not_20_out, not_21_out, not_22_out, not_23_out, not_24_out, not_25_out, not_26_out,
       not_27_out, not_28_out, not_29_out, not_30_out, not_31_out, not_32_out, not_33_out, not_34_out,
       not_35_out, not_36_out, not_37_out, not_38_out, not_39_out, not_40_out, not_41_out, not_42_out,
       not_43_out, not_44_out, not_45_out, not_46_out, not_47_out, not_48_out, not_49_out, not_50_out,
       not_51_out, not_52_out, not_53_out, not_54_out, not_55_out, not_56_out;

  not not_1 (not_1_out, x3);
  not not_2 (not_2_out, x1);
  not not_3 (not_3_out, x0);
  not not_4 (not_4_out, x3);
  not not_5 (not_5_out, x3);
  not not_6 (not_6_out, x2);
  not not_7 (not_7_out, x1);
  not not_8 (not_8_out, x2);
  not not_9 (not_9_out, x0);
  not not_10 (not_10_out, x3);
  not not_11 (not_11_out, x1);
  not not_12 (not_12_out, x2);
  not not_13 (not_13_out, x1);
  not not_14 (not_14_out, x3);
  not not_15 (not_15_out, x2);
  not not_16 (not_16_out, x0);
  not not_17 (not_17_out, x3);
  not not_18 (not_18_out, x2);
  and and_1 (and_1_out, not_17_out, not_18_out, x0);
  not not_19 (not_19_out, x3);
  and and_2 (and_2_out, not_19_out, x2, not_20_out);
  not not_20 (not_20_out, x0);
  not not_21 (not_21_out, x3);
  and and_3 (and_3_out, not_21_out, x2, x1);
  not not_22 (not_22_out, x2);
  and and_4 (and_4_out, x3, not_22_out, not_23_out);
  not not_23 (not_23_out, x1);
  and and_5 (and_5_out, x3, not_24_out, not_25_out);
  not not_24 (not_24_out, x2);
  not not_25 (not_25_out, x0);
  not not_26 (not_26_out, x3);
  and and_6 (and_6_out, not_26_out, not_27_out, x0);
  not not_27 (not_27_out, x2);
  not not_28 (not_28_out, x3);
  and and_7 (and_7_out, not_28_out, not_29_out, x1);
  not not_29 (not_29_out, x2);
  not not_30 (not_30_out, x3);
  and and_8 (and_8_out, not_30_out, x2, not_31_out);
  not not_31 (not_31_out, x1);
  and and_9 (and_9_out, x3, not_32_out, not_33_out);
  not not_32 (not_32_out, x2);
  not not_33 (not_33_out, x1);
  and and_10 (and_10_out, x3, not_34_out, not_35_out);
  not not_34 (not_34_out, x2);
  not not_35 (not_35_out, x0);
  not not_36 (not_36_out, x2);
  not not_37 (not_37_out, x1);
  and and_11 (and_11_out, not_36_out, not_37_out, x0);
  not not_38 (not_38_out, x3);
  and and_12 (and_12_out, not_38_out, x1, x0);
  not not_39 (not_39_out, x2);
  not not_40 (not_40_out, x1);
  not not_41 (not_41_out, x3);
  not not_42 (not_42_out, x3);
  not not_43 (not_43_out, x0);
  not not_44 (not_44_out, x2);
  not not_45 (not_45_out, x0);
  not not_46 (not_46_out, x3);
  and and_13 (and_13_out, not_46_out, not_47_out, x0);
  not not_47 (not_47_out, x1);
  not not_48 (not_48_out, x2);
  and and_14 (and_14_out, not_48_out, x1, not_49_out);
  not not_49 (not_49_out, x0);
  not not_50 (not_50_out, x3);
  and and_15 (and_15_out, not_50_out, x2);
  not not_51 (not_51_out, x2);
  and and_16 (and_16_out, x3, not_51_out, not_52_out);
  not not_52 (not_52_out, x1);
  not not_53 (not_53_out, x3);
  not not_54 (not_54_out, x2);
  not not_55 (not_55_out, x1);
  not not_56 (not_56_out, x0);
  and and_17 (and_17_out, not_1_out, not_2_out, not_3_out);
  and and_18 (and_18_out, not_4_out, x1, x0);
  and and_19 (and_19_out, not_5_out, x2);
  and and_20 (and_20_out, x3, not_6_out, not_7_out, x0);
  and and_21 (and_21_out, x3, not_8_out, x1, not_9_out);
  and and_22 (and_22_out, not_10_out, not_11_out, x0);
  and and_23 (and_23_out, not_12_out, not_13_out, x0);
  and and_24 (and_24_out, not_14_out, x2, x1);
  and and_25 (and_25_out, x3, not_15_out, x1, not_16_out);
  or or_1 (y2, and_1_out, and_2_out, and_3_out, and_4_out, and_5_out);
  or or_2 (y3, and_6_out, and_7_out, and_8_out, and_9_out, and_10_out);
  or or_3 (y4, and_11_out, and_12_out);
  and and_26 (and_26_out, not_39_out, not_40_out, x0);
  and and_27 (and_27_out, not_41_out, x1, x0);
  and and_28 (and_28_out, not_42_out, x2, not_43_out);
  and and_29 (and_29_out, x3, not_44_out, x1, not_45_out);
  or or_4 (y6, and_13_out, and_14_out, and_15_out, and_16_out);
  and and_30 (and_30_out, not_53_out, not_54_out, not_55_out, not_56_out);
  and and_31 (and_31_out, x3, x1, x0);
  or or_5 (y7, and_30_out, and_31_out, and_32_out);
  and and_32 (and_32_out, x3, x2);
  or or_6 (y0, and_17_out, and_18_out, and_19_out, and_20_out, and_21_out);
  or or_7 (y1, and_22_out, and_23_out, and_24_out, and_25_out);
  or or_8 (y5, and_26_out, and_27_out, and_28_out, and_29_out);
endmodule

module CD (
  input  x0,
  input  x1,
  input  x2,
  input  x3,
  input  x4,
  input  x5,
  input  x6,
  input  x7,
  input  x8,
  input  x9,
  output y3,
  output y2,
  output y1,
  output y0
);

  or or_1 (y3, x9, x8, x7);
  or or_2 (y2, x6, x5, x4, x3);
  or or_3 (y1, x9, x6, x5, x2, x1);
  or or_4 (y0, x8, x6, x4, x2, x0);
endmodule
