// Logisim project ИЛИ-НЕ и И-НЕ.circ as structural Verilog: 1 circuit, main circuit main
module main (
  input  in1,
  input  in2,
  input  in,
  input  in_2,
  output out,
  output out_2
);

  wire transistor_1_out, transistor_3_out, transistor_7_out, transistor_8_out;

  Transistor #(.\type ("n")) transistor_1 (.in(1'b1), .out(transistor_1_out), .gate(in));
  Transistor transistor_2 (.in(transistor_3_out), .out(transistor_1_out), .gate(in));
  Transistor transistor_3 (.in(1'b0), .out(transistor_3_out), .gate(in_2));
  Transistor #(.\type ("n")) transistor_4 (.in(1'b1), .out(transistor_3_out), .gate(in_2));
  Transistor #(.gate("br")) transistor_5 (.in(1'b1), .out(out), .gate(transistor_1_out));
  Transistor #(.\type ("n")) transistor_6 (.in(1'b0), .out(out), .gate(transistor_1_out));
  Transistor transistor_7 (.in(1'b0), .out(transistor_7_out), .gate(in1));
  Transistor #(.\type ("n")) transistor_8 (.in(1'b1), .out(transistor_8_out), .gate(in1));
  Transistor #(.\type ("n")) transistor_9 (.in(transistor_8_out), .out(transistor_7_out), .gate(in2));
  Transistor transistor_10 (.in(1'b0), .out(transistor_7_out), .gate(in2));
  Transistor #(.gate("br")) transistor_11 (.in(1'b1), .out(out_2), .gate(transistor_7_out));
  Transistor #(.\type ("n")) transistor_12 (.in(1'b0), .out(out_2), .gate(transistor_7_out));

  // Notes on the sheet:
  //   n - type
  //   p - type
  //   p - type
  //   n - type
  //   ИЛИ-НЕ
  //   n - type
  //   n - type 
  //   n - type 
  //   p - type 
  //   И-НЕ
  //   p - type 
  //   p - type 
  //   n - type 
endmodule
