// Logisim project Инвертор.circ as structural Verilog: 1 circuit, main circuit main
module main (
  input  in_1,
  input  [7:0] \input ,
  output [7:0] out
);

  xor xor_1 (out[0], \input [0], in_1);
  xor xor_2 (out[1], \input [1], in_1);
  xor xor_3 (out[2], \input [2], in_1);
  xor xor_4 (out[3], \input [3], in_1);
  xor xor_5 (out[4], \input [4], in_1);
  xor xor_6 (out[5], \input [5], in_1);
  xor xor_7 (out[6], \input [6], in_1);
  xor xor_8 (out[7], \input [7], in_1);

  // Notes on the sheet:
  //   ИНВЕРТОР
endmodule
