// Logisim project Регистр сдвига.circ as structural Verilog: 1 circuit, main circuit main
module main (
  input  [3:0] in,
  input  \вкл ,
  output [7:0] out_3
);

  wire and_1_out, button_1_out, clock_1_out, d_ff_2_qn, multiplexer_1_out, nor_1_out, not_1_out, or_1_out,
       or_2_out, xor_1_out;
  wire [1:0] d_ff_1_q;

  or or_1 (or_1_out, d_ff_1_q[1], d_ff_2_qn);
  not not_1 (not_1_out, d_ff_2_qn);
  D_Flip_Flop d_ff_1 (.clk(and_1_out), .D(or_1_out), .Q(d_ff_1_q[0]), .reset(or_2_out));  // open: Qn, preset, en
  or or_2 (or_2_out, xor_1_out, button_1_out);
  xor xor_1 (xor_1_out, not_1_out, d_ff_1_q[1]);
  Clock clock_1 (.out(clock_1_out));
  Multiplexer #(.select(2)) multiplexer_1 (
    .in0(in[0]), .in1(in[1]), .in2(in[2]), .in3(in[3]), .out(multiplexer_1_out), .sel(d_ff_1_q));  // open: en
  and and_1 (and_1_out, clock_1_out, \вкл );
  D_Flip_Flop d_ff_2 (
    .clk(and_1_out), .D(d_ff_1_q[0]), .Q(d_ff_1_q[1]), .Qn(d_ff_2_qn), .en(d_ff_1_q[0]), .reset(button_1_out));  // open: preset
  Button button_1 (.out(button_1_out));
  nor nor_1 (nor_1_out, clock_1_out, out_3[0]);
  D_Flip_Flop d_ff_3 (
    .clk(nor_1_out), .D(multiplexer_1_out), .Q(out_3[7]), .en(\вкл ), .reset(button_1_out));  // open: Qn, preset
  D_Flip_Flop d_ff_4 (
    .clk(nor_1_out), .D(out_3[7]), .Q(out_3[6]), .en(\вкл ), .reset(button_1_out));  // open: Qn, preset
  D_Flip_Flop d_ff_5 (
    .clk(nor_1_out), .D(out_3[6]), .Q(out_3[5]), .en(\вкл ), .reset(button_1_out));  // open: Qn, preset
  D_Flip_Flop d_ff_6 (
    .clk(nor_1_out), .D(out_3[5]), .Q(out_3[4]), .en(\вкл ), .reset(button_1_out));  // open: Qn, preset
  D_Flip_Flop d_ff_7 (
    .clk(nor_1_out), .D(out_3[4]), .Q(out_3[3]), .en(\вкл ), .reset(button_1_out));  // open: Qn, preset
  D_Flip_Flop d_ff_8 (
    .clk(nor_1_out), .D(out_3[3]), .Q(out_3[2]), .en(\вкл ), .reset(button_1_out));  // open: Qn, preset
  D_Flip_Flop d_ff_9 (
    .clk(nor_1_out), .D(out_3[2]), .Q(out_3[1]), .en(\вкл ), .reset(button_1_out));  // open: Qn, preset
  D_Flip_Flop d_ff_10 (
    .clk(nor_1_out), .D(out_3[1]), .Q(out_3[0]), .en(\вкл ), .reset(button_1_out));  // open: Qn, preset

  // Notes on the sheet:
  //   Регистр сдвига
  //   сбросить
  //   result
endmodule
